# Fritzing sketch R01_3 sensores_N1 (saved by Fritzing 0.9.3b)
breadboards: 1

parts:
  Componente4 = Arduino Uno (Rev3)
  part = Resistor [tolerance=±5% resistance=4.7k package="2010 [SMD]"]
  DS1 = DS18B20 adaptado
  DS2 = DS18B20 adaptado
  DS3 = DS18B20 adaptado

nets:
  N1: Componente4.D2, part.Pin_1, DS1.DQ, DS2.DQ, DS3.DQ
  VDD: Componente4.5V, part.Pin_0, DS1.VDD, DS2.VDD, DS3.VDD
  GND: Componente4.GND, DS1.GND, DS2.GND, DS3.GND
